# Fritzing sketch humidifier (saved by Fritzing 0.9.3b)
perfboards: 1

parts:
  Q1 = NPN-Transistor [package="TO92 [THT]"]
  Raspberry_Pi_B_rev1 = Raspberry Pi B rev1
  USB_Power_Cable = USB connector [package=THT]
  Humidifier_Power = mystery part, 3 pins [chip_label=?]
  D1 = Diode [package=diode-1n4001]
  part = Resistor [tolerance=±5% resistance=1k package=THT]
  part_2 = Resistor [tolerance=±0.05% resistance=10k package="1206 [SMD]"]
  Humidifier_LEDs = RGB LED - (4 legs) [package="5 mm [THT]"]
  Relay = OMRON PCB Power Relay – G5LE [part_number="G5LE-1\n" package=THT]

nets:
  N1: Q1.E, Raspberry_Pi_B_rev1.GND, part_2.Pin_0, Humidifier_LEDs.common_anode
  N2: Q1.B, part.Pin_1, part_2.Pin_1
  N3: Q1.C, D1.A, Relay.COIL2
  N4: Raspberry_Pi_B_rev1.5V, D1.C, Relay.COIL1
  N5: Raspberry_Pi_B_rev1.GPIO_15, part.Pin_0
  N6: Raspberry_Pi_B_rev1.GPIO_10, Humidifier_LEDs.red_cathode
  N7: Raspberry_Pi_B_rev1.GPIO_9, Humidifier_LEDs.blue_cathode
  N8: USB_Power_Cable.5V, Humidifier_Power.pin3
  N9: USB_Power_Cable.chassis5, Relay.C
  N10: Humidifier_Power.pin1, Relay.B

notes:
  (USB power cable included with humidifier)
  ---------------------------------------------- Humidifier Internal ----------------------------------------------
